// Logisim project SimpleCPU.circ as structural Verilog: 11 circuits, main circuit main
module main (
  input  resetProgram
);

  wire and_1_out, controlunit_1_isalu, controlunit_1_isflow, controlunit_1_islogic, controlunit_1_ismem,
       flow_1_set, memory_1_load, memory_1_loadi, memory_1_push, memory_1_set, not_1_out, not_2_out,
       or_1_out, or_2_out, or_3_out, programClock_out;
  wire [3:0] controlunit_1_aluindex, controlunit_1_flowindex, controlunit_1_logicindex,
       controlunit_1_memoryindex, flow_1_outval, instructioncounter_1_count, registersv2_1_areg,
       registersv2_1_areg_2;
  wire [7:0] alu_1_outval, controlled_buffer_2_out, controlled_buffer_3_out, controlunit_1_regaddra,
       controlunit_1_regaddrb, controlunit_1_regaddrc, logic_1_outval, memory_1_addr, memory_1_outval,
       registersv2_1_breg, registersv2_1_creg;
  wire [31:0] rom_1_data;

  Clock programClock (.out(programClock_out));
  not not_1 (not_1_out, programClock_out);
  ROM #(.addrWidth(4), .dataWidth(32)) rom_1 (.addr(instructioncounter_1_count), .data(rom_1_data));
  InstructionCounter instructioncounter_1 (
    .value(flow_1_outval), .set(flow_1_set), .clock(programClock_out), .reset(resetProgram),
    .count(instructioncounter_1_count));
  RAM ram_1 (.addr(memory_1_addr), .we(or_1_out), .oe(1'b1), .clk(not_1_out), .din(memory_1_outval));  // open: dout
  registersv2 registersv2_1 (
    .Aaddr(controlunit_1_regaddra), .Baddr(controlunit_1_regaddrb), .Caddr(controlunit_1_regaddrc),
    .Value(controlled_buffer_3_out), .WE(1'b1), .clock(not_1_out), .reset(resetProgram),
    .Areg({registersv2_1_areg_2, registersv2_1_areg}), .Breg(registersv2_1_breg), .Creg(registersv2_1_creg));
  buf or_1 (or_1_out, or_2_out);  // OR_Gate
  Hex_Digit_Display hex_digit_display_1 (.value(registersv2_1_areg_2));  // open: dp
  not not_2 (not_2_out, or_3_out);
  Hex_Digit_Display hex_digit_display_2 (.value(registersv2_1_areg));  // open: dp
  ControlUnit controlunit_1 (
    .OpCode(rom_1_data[31:24]), .Ain(rom_1_data[23:16]), .Bin(rom_1_data[15:8]), .Cin(rom_1_data[7:0]),
    .ALUindex(controlunit_1_aluindex), .IsALU(controlunit_1_isalu), .LOGICindex(controlunit_1_logicindex),
    .IsLogic(controlunit_1_islogic), .FLOWindex(controlunit_1_flowindex), .IsFLOW(controlunit_1_isflow),
    .MEMORYindex(controlunit_1_memoryindex), .IsMEM(controlunit_1_ismem), .RegAddrA(controlunit_1_regaddra),
    .RegAddrB(controlunit_1_regaddrb), .RegAddrC(controlunit_1_regaddrc));  // open: MemVal
  assign controlunit_1_regaddrb = not_2_out ? registersv2_1_breg : 8'bz;  // Controlled_Buffer controlled_buffer_1
  assign controlled_buffer_2_out = or_3_out ? controlunit_1_regaddrb : 8'bz;  // Controlled_Buffer controlled_buffer_2
  MEMORY memory_1 (
    .index(controlunit_1_memoryindex), .reg1val(controlunit_1_regaddra), .reg2val(controlled_buffer_2_out),
    .IsMemory(controlunit_1_ismem), .outVal(memory_1_outval), .addr(memory_1_addr), .SET(memory_1_set),
    .LOAD(memory_1_load), .LOADi(memory_1_loadi), .PUSH(memory_1_push));  // open: MOV, STORE, STOREi, POP
  or or_2 (or_2_out, memory_1_load, memory_1_loadi, memory_1_push);
  ALU alu_1 (
    .index(controlunit_1_aluindex), .reg1val(registersv2_1_breg), .reg2val(registersv2_1_creg),
    .outVal(alu_1_outval));
  assign controlled_buffer_3_out = controlunit_1_isalu ? alu_1_outval : 8'bz;  // Controlled_Buffer controlled_buffer_3
  LOGIC logic_1 (
    .index(controlunit_1_logicindex), .reg1val(registersv2_1_breg), .reg2val(registersv2_1_creg),
    .outVal(logic_1_outval));
  assign controlled_buffer_3_out = controlunit_1_islogic ? logic_1_outval : 8'bz;  // Controlled_Buffer controlled_buffer_4
  FLOW flow_1 (
    .index(controlunit_1_flowindex), .labelAddress(controlunit_1_regaddra), .reg1val(registersv2_1_breg),
    .reg2val(registersv2_1_creg), .isFlow(controlunit_1_isflow), .outVal(flow_1_outval), .set(flow_1_set));
  assign controlled_buffer_3_out = and_1_out ? memory_1_outval : 8'bz;  // Controlled_Buffer controlled_buffer_5
  buf or_3 (or_3_out, memory_1_set);  // OR_Gate
  and and_1 (and_1_out, controlunit_1_ismem, or_3_out);

  // Notes on the sheet:
  //   starts high
  //   contents of rom_1 (hex, n*v repeats v):
  //   4000fe00
  //   regAddrB = val
endmodule

module fulladder (
  input  a,
  input  b,
  input  carryin,
  output carryout,
  output sum
);

  wire n7408_1_pin3, n7408_1_pin4, n7408_1_pin6;

  _7408 #(.ShowInternalStructure("true")) u_7408_1 (
    .pin1(a), .pin2(b), .pin3(n7408_1_pin3), .pin4(n7408_1_pin4), .pin5(carryin), .pin6(n7408_1_pin6));  // open: pin13, pin12, pin11, pin10, pin9, pin8
  _7486 #(.ShowInternalStructure("true")) u_7486_1 (
    .pin13(b), .pin12(a), .pin11(n7408_1_pin4), .pin10(n7408_1_pin4), .pin9(carryin), .pin8(sum));  // open: pin1, pin2, pin3, pin4, pin5, pin6
  _7432 #(.ShowInternalStructure("true")) u_7432_1 (
    .pin1(n7408_1_pin6), .pin2(n7408_1_pin3), .pin3(carryout));  // open: pin4, pin5, pin6, pin13, pin12, pin11, pin10, pin9, pin8
endmodule

module ALU (
  input  [3:0] index,
  input  [7:0] reg1val,
  input  [7:0] reg2val,
  output [7:0] outVal
);

  wire [0:0] undriven;
  wire [7:0] adder_1_out, comparator_1_eq, comparator_1_gt, comparator_1_lt, divider_1_out, multiplier_1_out,
       subtractor_1_out;
  wire [7:7] undriven_2;

  Adder adder_1 (.a(reg1val), .b(reg2val), .out(adder_1_out));  // open: cin, cout
  Subtractor subtractor_1 (.a(reg1val), .b(reg2val), .out(subtractor_1_out));  // open: bin, bout
  Multiplier multiplier_1 (.a(reg1val), .b(reg2val), .out(multiplier_1_out));  // open: cin, cout
  Divider divider_1 (.a(reg1val), .b(reg2val), .out(divider_1_out));  // open: upper, rem
  Comparator comparator_1 (
    .a(reg1val), .b(reg2val), .gt(comparator_1_gt[0]), .eq(comparator_1_eq[0]), .lt(comparator_1_lt[0]));
  Multiplexer #(.select(4), .width(8)) multiplexer_1 (
    .in0(adder_1_out), .in1(subtractor_1_out), .in2(multiplier_1_out), .in3(divider_1_out),
    .in4({reg1val[6:0], undriven[0]}), .in5({undriven_2[7], reg1val[7:1]}), .in6(comparator_1_gt),
    .in7(comparator_1_eq), .in8(comparator_1_lt), .out(outVal), .sel(index));  // open: in9, in10, in11, in12, in13, in14, in15
endmodule

module InstructionCounter (
  input  [3:0] value,
  input  set,
  input  clock,
  input  reset,
  output [3:0] count
);

  wire and_1_out, and_2_out, and_3_out, and_4_out, and_5_out, and_6_out, and_7_out, and_8_out, j_k_ff_1_qn,
       not_1_out, not_2_out, not_3_out, not_4_out, or_1_out, or_2_out, or_3_out, or_4_out, t_ff_1_qn,
       t_ff_2_qn, t_ff_3_qn, undriven;

  not not_1 (not_1_out, value[1]);
  not not_2 (not_2_out, value[2]);
  not not_3 (not_3_out, value[3]);
  not not_4 (not_4_out, value[0]);
  T_Flip_Flop t_ff_1 (.T(1'b1), .clk(clock), .Q(count[0]), .Qn(t_ff_1_qn), .reset(or_1_out), .preset(and_2_out));
  and and_1 (and_1_out, set, not_4_out);
  or or_1 (or_1_out, and_1_out, reset);
  J_K_Flip_Flop j_k_ff_1 (.J(1'b1), .K(1'b1), .clk(undriven), .Qn(j_k_ff_1_qn));  // open: Q, preset, reset
  and and_2 (and_2_out, value[0], set);
  T_Flip_Flop t_ff_2 (.T(1'b1), .clk(t_ff_1_qn), .Q(count[1]), .Qn(t_ff_2_qn), .reset(or_2_out), .preset(and_4_out));
  or or_2 (or_2_out, and_3_out, reset);
  and and_3 (and_3_out, set, not_1_out);
  and and_4 (and_4_out, value[1], set);
  T_Flip_Flop t_ff_3 (.T(1'b1), .clk(t_ff_2_qn), .Q(count[2]), .Qn(t_ff_3_qn), .reset(or_3_out), .preset(and_6_out));
  or or_3 (or_3_out, and_5_out, reset);
  and and_5 (and_5_out, set, not_2_out);
  J_K_Flip_Flop j_k_ff_2 (.J(1'b1), .K(1'b1), .clk(j_k_ff_1_qn));  // open: Q, Qn, preset, reset
  and and_6 (and_6_out, value[2], set);
  T_Flip_Flop t_ff_4 (.T(1'b1), .clk(t_ff_3_qn), .Q(count[3]), .reset(or_4_out), .preset(and_8_out));  // open: Qn
  or or_4 (or_4_out, and_7_out, reset);
  and and_7 (and_7_out, set, not_3_out);
  and and_8 (and_8_out, value[3], set);
endmodule

module registers (
  input  [1:0] A,
  input  [1:0] B,
  input  [7:0] WriteAVal,
  input  [7:0] WriteBVal,
  input  clock,
  input  WEa,
  input  WEb,
  output [7:0] Aout,
  output [7:0] Bout
);

  wire demultiplexer_1_out0, demultiplexer_1_out1, demultiplexer_1_out2, demultiplexer_1_out3,
       demultiplexer_2_out0, demultiplexer_2_out1, demultiplexer_2_out2, demultiplexer_2_out3, or_1_out,
       or_2_out, or_3_out, or_4_out;
  wire [7:0] demultiplexer_3_out0, demultiplexer_3_out1, demultiplexer_3_out2, demultiplexer_3_out3,
       demultiplexer_4_out0, demultiplexer_4_out1, demultiplexer_4_out2, demultiplexer_4_out3, or_5_out,
       or_6_out, or_7_out, or_8_out, register_1_q, register_2_q, register_3_q, register_4_q;

  Demultiplexer #(.select(2)) demultiplexer_1 (
    .out0(demultiplexer_1_out0), .out1(demultiplexer_1_out1), .out2(demultiplexer_1_out2),
    .out3(demultiplexer_1_out3), .in(WEb), .sel(B));
  Demultiplexer #(.select(2)) demultiplexer_2 (
    .out0(demultiplexer_2_out0), .out1(demultiplexer_2_out1), .out2(demultiplexer_2_out2),
    .out3(demultiplexer_2_out3), .in(WEa), .sel(A));
  Demultiplexer #(.select(2), .width(8)) demultiplexer_3 (
    .out0(demultiplexer_3_out0), .out1(demultiplexer_3_out1), .out2(demultiplexer_3_out2),
    .out3(demultiplexer_3_out3), .in(WriteAVal), .sel(A));
  Demultiplexer #(.select(2), .width(8)) demultiplexer_4 (
    .out0(demultiplexer_4_out0), .out1(demultiplexer_4_out1), .out2(demultiplexer_4_out2),
    .out3(demultiplexer_4_out3), .in(WriteBVal), .sel(B));
  or or_1 (or_1_out, demultiplexer_1_out0, demultiplexer_2_out0);
  or or_2 (or_2_out, demultiplexer_1_out1, demultiplexer_2_out1);
  or or_3 (or_3_out, demultiplexer_1_out2, demultiplexer_2_out2);
  or or_4 (or_4_out, demultiplexer_1_out3, demultiplexer_2_out3);
  assign or_5_out = demultiplexer_3_out0 | demultiplexer_4_out0;  // OR_Gate or_5, 8 bits wide
  assign or_6_out = demultiplexer_3_out2 | demultiplexer_4_out2;  // OR_Gate or_6, 8 bits wide
  assign or_7_out = demultiplexer_3_out3 | demultiplexer_4_out3;  // OR_Gate or_7, 8 bits wide
  Register register_1 (.D(or_5_out), .en(or_1_out), .clk(clock), .Q(register_1_q));  // open: clr
  assign or_8_out = demultiplexer_3_out1 | demultiplexer_4_out1;  // OR_Gate or_8, 8 bits wide
  Register register_2 (.D(or_8_out), .en(or_2_out), .clk(clock), .Q(register_2_q));  // open: clr
  Register register_3 (.D(or_6_out), .en(or_3_out), .clk(clock), .Q(register_3_q));  // open: clr
  Register register_4 (.D(or_7_out), .en(or_4_out), .clk(clock), .Q(register_4_q));  // open: clr
  Multiplexer #(.select(2), .width(8)) multiplexer_1 (
    .in0(register_1_q), .in1(register_2_q), .in2(register_3_q), .in3(register_4_q), .out(Aout), .sel(A));
  Multiplexer #(.select(2), .width(8)) multiplexer_2 (
    .in0(register_1_q), .in1(register_2_q), .in2(register_3_q), .in3(register_4_q), .out(Bout), .sel(B));
endmodule

module registersv2 (
  input  [7:0] Aaddr,
  input  [7:0] Baddr,
  input  [7:0] Caddr,
  input  [7:0] Value,
  input  WE,
  input  clock,
  input  reset,
  output [7:0] Areg,
  output [7:0] Breg,
  output [7:0] Creg
);

  wire demultiplexer_1_out0, demultiplexer_1_out1, demultiplexer_1_out2, demultiplexer_1_out3,
       demultiplexer_1_out4, demultiplexer_1_out5, demultiplexer_1_out6, demultiplexer_1_out7;
  wire [7:0] register_1_q, register_2_q, register_3_q, register_4_q, register_5_q, register_6_q,
       register_7_q, register_8_q, register_9_q;

  Demultiplexer #(.select(4)) demultiplexer_1 (
    .out0(demultiplexer_1_out0), .out1(demultiplexer_1_out1), .out2(demultiplexer_1_out2),
    .out3(demultiplexer_1_out3), .out4(demultiplexer_1_out4), .out5(demultiplexer_1_out5),
    .out6(demultiplexer_1_out6), .out7(demultiplexer_1_out7), .in(WE), .sel(Aaddr[3:0]));  // open: out8, out9, out10, out11, out12, out13, out14, out15
  Register register_1 (.D(Value), .en(demultiplexer_1_out0), .clk(clock), .Q(register_1_q), .clr(reset));
  Register register_2 (.D(Value), .en(demultiplexer_1_out1), .clk(clock), .Q(register_2_q), .clr(reset));
  Register register_3 (.D(Value), .en(demultiplexer_1_out2), .clk(clock), .Q(register_3_q), .clr(reset));
  Register register_4 (.D(Value), .en(demultiplexer_1_out3), .clk(clock), .Q(register_4_q), .clr(reset));
  Register register_5 (.D(Value), .en(demultiplexer_1_out4), .clk(clock), .Q(register_5_q), .clr(reset));
  Register register_6 (.D(Value), .en(demultiplexer_1_out5), .clk(clock), .Q(register_6_q), .clr(reset));
  Register register_7 (.D(Value), .en(demultiplexer_1_out6), .clk(clock), .Q(register_7_q), .clr(reset));
  Register register_8 (.D(Value), .en(demultiplexer_1_out7), .clk(clock), .Q(register_8_q), .clr(reset));
  Register register_9 (.D(Value), .en(demultiplexer_1_out7), .clk(clock), .Q(register_9_q), .clr(reset));
  Multiplexer #(.select(4), .width(8)) multiplexer_1 (
    .in0(register_1_q), .in1(register_2_q), .in2(register_3_q), .in3(register_4_q), .in4(register_5_q),
    .in5(register_6_q), .in6(register_7_q), .in7(register_8_q), .in8(register_9_q), .out(Areg),
    .sel(Aaddr[3:0]));  // open: in9, in10, in11, in12, in13, in14, in15
  Multiplexer #(.select(4), .width(8)) multiplexer_2 (
    .in0(register_1_q), .in1(register_2_q), .in2(register_3_q), .in3(register_4_q), .in4(register_5_q),
    .in5(register_6_q), .in6(register_7_q), .in7(register_8_q), .in8(register_9_q), .in9({8{1'b1}}),
    .in10({8{1'b1}}), .in11({8{1'b1}}), .in12({8{1'b1}}), .in13({8{1'b1}}), .in14({8{1'b1}}),
    .in15({8{1'b1}}), .out(Breg), .sel(Baddr[3:0]));
  Multiplexer #(.select(4), .width(8)) multiplexer_3 (
    .in0(register_1_q), .in1(register_2_q), .in2(register_3_q), .in3(register_4_q), .in4(register_5_q),
    .in5(register_6_q), .in6(register_7_q), .in7(register_8_q), .in8(register_9_q), .out(Creg),
    .sel(Caddr[3:0]));  // open: in9, in10, in11, in12, in13, in14, in15

  // Notes on the sheet:
  //   0x09
endmodule

module ControlUnit (
  input  [7:0] OpCode,
  input  [7:0] Ain,
  input  [7:0] Bin,
  input  [7:0] Cin,
  output [3:0] ALUindex,
  output IsALU,
  output [3:0] LOGICindex,
  output IsLogic,
  output [3:0] FLOWindex,
  output IsFLOW,
  output [3:0] MEMORYindex,
  output IsMEM,
  output [7:0] RegAddrA,
  output [7:0] RegAddrB,
  output [7:0] RegAddrC,
  output [7:0] MemVal
);

  wire [7:0] demultiplexer_1_out4;

  Demultiplexer #(.select(3), .width(8)) demultiplexer_1 (
    .out0(RegAddrB), .out1(RegAddrB), .out2(RegAddrB), .out3(RegAddrB), .out4(demultiplexer_1_out4),
    .in(Bin), .sel(OpCode[2:0]));  // open: out5, out6, out7
  Demultiplexer #(.select(4), .width(4)) demultiplexer_2 (
    .out1(ALUindex), .out2(LOGICindex), .out3(FLOWindex), .out4(MEMORYindex), .in(OpCode[3:0]),
    .sel(OpCode[7:4]));  // open: out0, out5, out6, out7, out8, out9, out10, out11, out12, out13, out14, out15
  Demultiplexer #(.select(4)) demultiplexer_3 (
    .out1(IsALU), .out2(IsLogic), .out3(IsFLOW), .out4(IsMEM), .in(1'b1), .sel(OpCode[7:4]));  // open: out0, out5, out6, out7, out8, out9, out10, out11, out12, out13, out14, out15
  Demultiplexer #(.select(4), .width(8)) demultiplexer_4 (
    .out0(MemVal), .out1(MemVal), .out2(MemVal), .out3(MemVal), .out4(MemVal), .out5(MemVal), .out6(MemVal),
    .out7(MemVal), .in(demultiplexer_1_out4), .sel(OpCode[7:4]));  // open: out8, out9, out10, out11, out12, out13, out14, out15

  assign RegAddrA = Ain;
  assign RegAddrC = Cin;

  // Notes on the sheet:
  //   For operations in ISA with more than 8 bits
  //   When adding jump change this condition
endmodule

module OneHotState (
  input  clock,
  output Fetch,
  output Decode,
  output Execute,
  output Advance
);

  wire t_ff_1_qn;
  wire [1:0] t_ff_1_q;

  T_Flip_Flop t_ff_1 (.T(1'b1), .clk(clock), .Q(t_ff_1_q[0]), .Qn(t_ff_1_qn));  // open: reset, preset
  T_Flip_Flop t_ff_2 (.T(1'b1), .clk(t_ff_1_qn), .Q(t_ff_1_q[1]));  // open: Qn, reset, preset
  Demultiplexer #(.select(2)) demultiplexer_1 (
    .out0(Fetch), .out1(Decode), .out2(Execute), .out3(Advance), .in(1'b1), .sel(t_ff_1_q));
endmodule

module FLOW (
  input  [3:0] index,
  input  [7:0] labelAddress,
  input  [7:0] reg1val,
  input  [7:0] reg2val,
  input  isFlow,
  output [3:0] outVal,
  output set
);

  wire and_1_out, and_2_out, comparator_1_eq, comparator_2_eq, not_1_out;
  wire [3:0] controlled_buffer_1_out, controlled_buffer_2_out;

  Comparator comparator_1 (.a(reg1val), .b({8{1'b0}}), .eq(comparator_1_eq));  // open: gt, lt
  not not_1 (not_1_out, comparator_2_eq);
  Comparator comparator_2 (.a(reg1val), .b(reg2val), .eq(comparator_2_eq));  // open: gt, lt
  assign controlled_buffer_1_out = not_1_out ? labelAddress[3:0] : 4'bz;  // Controlled_Buffer controlled_buffer_1
  assign controlled_buffer_2_out = comparator_1_eq ? labelAddress[3:0] : 4'bz;  // Controlled_Buffer controlled_buffer_2
  and and_1 (and_1_out, comparator_1_eq, isFlow);
  and and_2 (and_2_out, not_1_out, isFlow);
  Multiplexer #(.select(2), .width(4)) multiplexer_1 (
    .in0(labelAddress[3:0]), .in1(controlled_buffer_2_out), .in2(controlled_buffer_1_out), .out(outVal),
    .sel(index[1:0]));  // open: in3
  Multiplexer #(.select(2)) multiplexer_2 (
    .in0(isFlow), .in1(and_1_out), .in2(and_2_out), .out(set), .sel(index[1:0]));  // open: in3

  // Notes on the sheet:
  //   This is a little bit not standard in that im passing the value instead of reg. addr since counter is outside in cpu
endmodule

module MEMORY (
  input  [3:0] index,
  input  [7:0] reg1val,
  input  [7:0] reg2val,
  input  IsMemory,
  output [7:0] outVal,
  output [7:0] addr,
  output SET,
  output MOV,
  output LOAD,
  output STORE,
  output LOADi,
  output STOREi,
  output PUSH,
  output POP
);

  Demultiplexer #(.select(4)) demultiplexer_1 (
    .out0(SET), .out1(MOV), .out2(LOAD), .out3(STORE), .out4(LOADi), .out5(STOREi), .out6(PUSH), .out7(POP),
    .in(IsMemory), .sel(index));  // open: out8, out9, out10, out11, out12, out13, out14, out15
  Multiplexer #(.select(4), .width(8)) multiplexer_1 (
    .in0(reg2val), .in2(reg2val), .in3(reg2val), .out(outVal), .sel(index));  // open: in1, in4, in5, in6, in7, in8, in9, in10, in11, in12, in13, in14, in15
  Multiplexer #(.select(4), .width(8)) multiplexer_2 (
    .in0(reg1val), .in2(reg1val), .out(addr), .sel(index));  // open: in1, in3, in4, in5, in6, in7, in8, in9, in10, in11, in12, in13, in14, in15

  // Notes on the sheet:
  //   r1
  //   r2
  //   set
  //   addr
  //   val
endmodule

module LOGIC (
  input  [3:0] index,
  input  [7:0] reg1val,
  input  [7:0] reg2val,
  output [7:0] outVal
);

  wire [7:0] and_1_out, nand_1_out, nor_1_out, not_1_out, or_1_out, shifter_1_out, xor_1_out;

  assign not_1_out = ~reg1val;  // NOT_Gate not_1, 8 bits wide
  assign and_1_out = reg1val & reg2val;  // AND_Gate and_1, 8 bits wide
  assign or_1_out = reg1val | reg2val;  // OR_Gate or_1, 8 bits wide
  assign nor_1_out = ~(reg1val | reg2val);  // NOR_Gate nor_1, 8 bits wide
  assign nand_1_out = ~(reg1val & reg2val);  // NAND_Gate nand_1, 8 bits wide
  assign xor_1_out = reg1val ^ reg2val;  // XOR_Gate xor_1, 8 bits wide
  Shifter shifter_1 (.in(reg1val), .\dist (reg2val[2:0]), .out(shifter_1_out));
  Multiplexer #(.select(4), .width(8)) multiplexer_1 (
    .in0(not_1_out), .in1(and_1_out), .in2(or_1_out), .in3(nor_1_out), .in4(nand_1_out), .in5(xor_1_out),
    .in6(shifter_1_out), .out(outVal), .sel(index));  // open: in7, in8, in9, in10, in11, in12, in13, in14, in15
endmodule
